// Digital circuit soc.dig as structural Verilog
module soc (
  input  [15:0] value,
  input  [1:0] dest,
  input  [1:0] src,
  input  R_R,
  output [4:0] rs,
  output [31:0] L,
  output [31:0] R,
  output [4:0] rd,
  output [3:0] pc,
  output [31:0] L_2,
  output [31:0] L_rs,
  output [15:0] R_rd,
  output [31:0] out_13
);

  wire add, add_out, advance_out, decoder_1_p1, decoder_1_p6, jmp, jmp_out, mode_out, undriven_4, undriven_5;
  wire [3:0] undriven_2;
  wire [31:0] fetch_1_d_inst, Program_d, undriven, undriven_3;

  Button u_add (.out(add_out));
  Button u_jmp (.out(jmp_out));
  LED programming (.in(mode_out));
  DipSwitch mode (.out(mode_out));
  EEPROMDualPort #(.AddrBits(4), .Bits(32)) Program (
    .A(undriven_2), .Din(undriven_3), .str(decoder_1_p1), .C(undriven_4), .ld(undriven_5), .D(Program_d));
  Button advance (.out(advance_out));
  fetch fetch_1 (
    .mode(mode_out), .D_stored(Program_d), .D_bypass(undriven), .C(advance_out), .value(L), .jump(jmp),
    .pc(pc), .D_inst(fetch_1_d_inst));
  LED add_2 (.in(add));
  LED jump (.in(jmp));
  // decoder decoder_1: pin names not known; wires that end beside it: decoder_1_p1, fetch_1_d_inst, L_rs, R_rd, rs, decoder_1_p6, rd, L, R, add, jmp
  execute execute_1 (.Op_1(L), .Op_2(R), .add(add), .result(out_13));
  // register_file register_file_1: pin names not known; wires that end beside it: rs, decoder_1_p6, rd, out_13, advance_out, L_rs, R_rd

  assign L_2 = L;

  // Notes on the sheet:
  //   contents of Program (hex, n*v repeats v):
  //   1,110001,8120000,8020000,8230000,8130000,8320000,8230000,7230006
endmodule
