// Digital circuit decoder.dig as structural Verilog
module decoder (
  input  [31:0] mode,
  input  [31:0] D_stored,
  input  [31:0] D_pgm,
  output [15:0] A,
  output [1:0] rs,
  output [1:0] rd
);

  wire [31:18] multiplexer_1_out;

  Multiplexer #(.Bits(32)) multiplexer_1 (
    .sel(mode[0]), .in_0(D_stored), .in_1(D_pgm),
    .out({multiplexer_1_out[31:22], rs, multiplexer_1_out[19:18], rd, A}));
  // Pins of 1 and 32 bits meet at mode

  // Notes on the sheet:
  //   mode: Take 32-bits input
  //   D_stored: Take 32-bits input
  //   D_pgm: Take 32-bits input
endmodule
