// Digital circuit execute.dig as structural Verilog
module execute (
  input  [15:0] A,
  input  [15:0] B,
  output [15:0] sum
);

  Add #(.Bits(16)) add_1 (.a(A), .b(B), .c_i(1'b0), .s(sum));  // open: c_o
endmodule
